# Fritzing sketch Replicape_B3 (saved by Fritzing 0.9.2b)

parts:
  BeagleBone1 = BeagleBone Black  # not connected
  End_stop_X = Hall effect end stop
  End_stop_Z = Hall effect end stop
  End_stop_Y = Hall effect end stop
  PSU = PSU [package="DIP (Dual Inline) [THT]"]
  Fan_0 = Stepper
  Stepper_Y = Stepper
  Stepper_E = Stepper
  Stepper_X = Stepper
  Stepper_Z = Stepper
  Replicape = DIP - 68 pins [chip_label=Replicape package="DIP (Dual Inline) [THT]"]
  Extruder_1 = Hotbed [package="DIP (Dual Inline) [THT]"]
  Hotbed = Hotbed [package="DIP (Dual Inline) [THT]"]
  U1 = TEMPERATURE-SENSOR [package=to-92]

nets:
  N1: End_stop_X.vcc, Replicape.pin57
  N2: End_stop_X.sig, Replicape.pin59
  N3: End_stop_X.gnd, Replicape.pin58
  N4: End_stop_Z.vcc, Replicape.pin51
  N5: End_stop_Z.sig, Replicape.pin53
  N6: End_stop_Z.gnd, Replicape.pin52
  N7: End_stop_Y.vcc, Replicape.pin54
  N8: End_stop_Y.sig, Replicape.pin56
  N9: End_stop_Y.gnd, Replicape.pin55
  N10: PSU.V+1, Replicape.pin12
  N11: PSU.V+2, Replicape.pin11
  N12: PSU.V-1, Replicape.pin10
  N13: PSU.V-2, Replicape.pin9
  N14: Fan_0.vcc, Replicape.pin34
  N15: Fan_0.gnd, Replicape.Fan_0_+
  N16: Stepper_Y.a+, Replicape.pin20
  N17: Stepper_Y.a-, Replicape.pin18
  N18: Stepper_Y.b+, Replicape.pin17
  N19: Stepper_Y.b-, Replicape.pin19
  N20: Stepper_E.a+, Replicape.pin28
  N21: Stepper_E.a-, Replicape.pin26
  N22: Stepper_E.b+, Replicape.pin25
  N23: Stepper_E.b-, Replicape.pin27
  N24: Stepper_X.a+, Replicape.pin16
  N25: Stepper_X.a-, Replicape.Stepper_x_B1
  N26: Stepper_X.b+, Replicape.Stepper_x_A1
  N27: Stepper_X.b-, Replicape.pin15
  N28: Stepper_Z.a+, Replicape.pin24
  N29: Stepper_Z.a-, Replicape.pin22
  N30: Stepper_Z.b+, Replicape.pin21
  N31: Stepper_Z.b-, Replicape.pin23
  N32: Replicape.HBP_heat_1, Hotbed.V-1
  N33: Replicape.HBP_heat_2, Hotbed.V-2
  N34: Replicape.pin5, Hotbed.V+1
  N35: Replicape.pin6, Hotbed.V+2
  N36: Replicape.pin7, Extruder_1.Heater_2
  N37: Replicape.pin8, Extruder_1.Heater_1
  N38: Replicape.pin35, Extruder_1.Fan_-
  N39: Replicape.pin36, Extruder_1.Fan_+
  N40: Replicape.pin62, Hotbed.Therm2
  N41: Replicape.pin63, Hotbed.Therm1
  N42: Replicape.pin65, Extruder_1.Therm_1
  N43: Replicape.pin66, U1.VCC
  N44: Replicape.pin67, U1.ADJ
  N45: Replicape.pin68, U1.GND

notes:
  Sig
  GND
  5V
  12V

custom parts:
  BeagleBone Black: BeagleBone Black rev. A5B
  Hall effect end stop: Hall effect end stop sensor
  PSU: 24V Power Supply Unit
  DIP - 68 pins: A DIP stand-in part for whatever IC you want. With 68 pins on a 300mil dual inline package (DIP) footprint.
  Hotbed: Hotbed with thermistor
  Hotbed: Hotbed with thermistor

// code stored in the sketch: Replicape.ino

